# Fritzing sketch CapstoneLora (saved by Fritzing 1.0.2b)
breadboards: 2

parts:
  REMOTE_STATION = Particle - Photon2
  Part1 = Adafruit PA1010D Mini GPS Module [part_number="Adafruit #4415"]
  Mod1 = RYLR896 [package=THT]
  M1 = BMP280
  A2 = Optical fine dust sensor
  BASE_STATION = Particle - Photon2
  Mod2 = RYLR896 [package=THT]

nets (from the schematic view):
  VCC: REMOTE_STATION.Pin_2, REMOTE_STATION.Pin_31, Part1.VCC, Mod1.pin1, M1.VIN, A2.Pin_4
  N1: REMOTE_STATION.Pin_4, REMOTE_STATION.Pin_32, A2.Pin_1
  N2: REMOTE_STATION.Pin_14, Mod1.pin3#3
  N3: REMOTE_STATION.Pin_15, Mod1.pin3#2
  N4: REMOTE_STATION.Pin_17, Part1.SDA, M1.SDA, A2.Pin_3
  N5: REMOTE_STATION.Pin_18, Part1.SCL, M1.SCL, A2.Pin_2
  N6: BASE_STATION.Pin_2, Mod2.pin1
  N7: BASE_STATION.Pin_4, Mod2.pin5
  N8: BASE_STATION.Pin_14, Mod2.pin3#3
  N9: BASE_STATION.Pin_15, Mod2.pin3#2

notes:
  Air Quality LoRa Comm

custom parts:
  Particle - Photon2: The Photon 2 is a microcontroller and Wi-Fi networking developed by particle. Features: 802.11a/b/g/n Wi-Fi, 2.4 GHz and 5 GHz Integrated PCB antenna Integrated U.FL connector for external antenna Integrated RF switch BLE 5 using same antenna as Wi-Fi Realtek RTL8721DM MCU ARM Cortex M33 CPU, 200 MHz 2048 KB (2 MB) user application maximum size 3072 KB (3 MB) of RAM available to user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
  Adafruit PA1010D Mini GPS Module: This miniature GPS breakout is only 1" x 1" (~ 25mm x 25mm) but houses a complete GPS/GNSS solution with both I2C and UART interfaces. There's even an antenna on top so it's plug and play! Support for GPS, GLONASS, GALILEO, QZSS -165 dBm sensitivity, up to 10 Hz updates Up to 210 PRN channels with 99 search channels and 33 simultaneous tracking channels 5V friendly design and only 30mA current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
  RYLR896: RYLR896 UART Interface 868/915mhz LORA Transceiver Module
  BMP280: Temperature Humidity Barometric presure Sensor, I2C
  Optical fine dust sensor: The HM3301 sensor determines the fine dust particle concentration in the air using the scattered light method from a particle size of 0.3 μm.
